# Fritzing sketch schema (saved by Fritzing 0.9.3b)

parts:
  U1 = LuaNode32 / ESP32
  SIM800L_BO1 = SIM800L BO
  C1 = Capacitor Polarized [package=panasonic_d]
  U2 = LIPO-110mAh [package=lipo-110]
  MIC1 = Microphone
  Součástka1 = Solar Cell
  TP1 = TP4056 [chip_label=TP4056 package="DIP (Dual Inline) [THT]"]
  Součástka2 = INA219 High Side DC Current Sensor Breakout [part_number=904]
  U3 = Mini-360 DC-DC Buck converter [package=THT]
  D1 = Zener Diode [part_number=1N4732A breakdown_voltage=3.6V package="Melf DO-213 AB [SMD]"]

nets:
  3V3: U1.3V3, Součástka2.VCC
  GND: U1.GND, TP1.pin2, Součástka2.GND, U3.OUT-
  N1: U1.RX2, SIM800L_BO1.pin_5
  N2: U1.TX2, SIM800L_BO1.pin_4
  N3: U1.D21, Součástka2.SDA
  N4: U1.D22, Součástka2.SCL
  N5: SIM800L_BO1.PIN2, C1.+, TP1.pin3
  N6: SIM800L_BO1.pin_6, C1.-, TP1.pin6
  N7: SIM800L_BO1.pin_9, MIC1.pin2
  N8: SIM800L_BO1.pin_10, MIC1.pin1
  N9: U2.+, TP1.pin4
  N10: U2.-, TP1.pin5
  N11: Součástka1.+, D1.anode
  N12: Součástka1.-, U3.IN-
  N13: TP1.pin1, Součástka2.VIN-
  N14: Součástka2.VIN+, U3.OUT+
  N15: U3.IN+, D1.cathode

custom parts:
  LuaNode32 / ESP32: ESP32 based LuaNode32
  TP4056: A DIP stand-in part for whatever IC you want. With 6 pins on a 300mil dual inline package (DIP) footprint.
  INA219 High Side DC Current Sensor Breakout: This breakout board will solve all your power-monitoring problems. Instead of struggling with two multimeters, you can just use the handy INA219B chip on this breakout to both measure both the high side voltage and DC current draw over I2C with 1% precision. Most current-measuring devices such as our current panel meter are only good for low side measuring. That means that unless you want to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
  Mini-360 DC-DC Buck converter: Mini-360 DC-DC Buck converter. Tiny buck step down voltage converter, input voltage 4.75 to 23V output 1 to 17V adjustable. Available from ebay and the like.
